# Fritzing sketch IRInLEDOut (saved by Fritzing 0.9.3b)
breadboards: 1

parts:
  Part1 = Arduino Uno (Rev3)
  IR1 = TSOP312.., 314.. [package=THT]
  R1 = Resistor [tolerance=±5% resistance=220 package=THT]
  R2 = Resistor [tolerance=±5% resistance=220 package=THT]
  R3 = Resistor [tolerance=±5% resistance=220 package="2512 [SMD]"]
  R4 = Resistor [tolerance=±5% resistance=220 package="2512 [SMD]"]
  R5 = Resistor [tolerance=±5% resistance=220 package="2512 [SMD]"]
  R6 = Resistor [tolerance=±5% resistance=220 package="2512 [SMD]"]
  R7 = Resistor [tolerance=±5% resistance=220 package=THT]
  R8 = Resistor [tolerance=±5% resistance=220 package=THT]
  R9 = Resistor [tolerance=±5% resistance=220 package=THT]
  LED1 = smd LED [color="Red (633nm)" package="0805 [SMD]"]
  LED2 = smd LED [color="Red (633nm)" package="0805 [SMD]"]
  LED3 = smd LED [color="Red (633nm)" package="0805 [SMD]"]
  LED4 = smd LED [color="Red (633nm)" package="0805 [SMD]"]
  LED5 = smd LED [color="Red (633nm)" package="0805 [SMD]"]
  LED6 = smd LED [color="Red (633nm)" package="0805 [SMD]"]
  LED7 = smd LED [color="Red (633nm)" package="0805 [SMD]"]
  LED8 = smd LED [color="Red (633nm)" package="0805 [SMD]"]
  LED9 = smd LED [color="Red (633nm)" package="0805 [SMD]"]

nets:
  N1: Part1.D8, R2.Pin_1
  N2: Part1.D9_PWM, R7.Pin_1
  N3: Part1.D10_PWM/SS, R8.Pin_1
  N4: Part1.D11_PWM/MOSI, R9.Pin_1
  N5: Part1.D2, IR1.GND
  N6: Part1.D3_PWM, R1.Pin_1
  N7: Part1.D4, R6.Pin_1
  N8: Part1.D5_PWM, R4.Pin_1
  N9: Part1.D6_PWM, R3.Pin_1
  N10: Part1.D7, R5.Pin_1
  N11: Part1.5V, IR1.Data
  N12: Part1.GND, IR1.Vs, LED1.cathode, LED2.cathode, LED3.cathode, LED4.cathode, LED5.cathode, LED6.cathode, LED7.cathode, LED8.cathode, LED9.cathode
  N13: R1.Pin_0, LED1.anode
  N14: R2.Pin_0, LED6.anode
  N15: R3.Pin_0, LED4.anode
  N16: R4.Pin_0, LED3.anode
  N17: R5.Pin_0, LED5.anode
  N18: R6.Pin_0, LED2.anode
  N19: R7.Pin_0, LED7.anode
  N20: R8.Pin_0, LED8.anode
  N21: R9.Pin_0, LED9.anode
